// Logisim project 816106.circ as structural Verilog: 5 circuits, main circuit main
module ALU (
  input  [15:0] A,
  input  [15:0] B,
  input  [1:0] T,
  output C,
  output Z,
  output N,
  output [15:0] S,
  output V
);

  wire and_1_out, and_2_out, B15, not_1_out, not_2_out, not_3_out;
  wire [14:0] xor_1_out;
  wire [15:0] adder_1_out, xor_2_out;

  assign {B15, xor_1_out} = B ^ {16{T[1]}};  // XOR_Gate xor_1, 16 bits wide
  Adder #(.width(16)) adder_1 (.a(A), .b({B15, xor_1_out}), .out(adder_1_out), .cin(T[1]), .cout(C));
  assign xor_2_out = B ^ A;  // XOR_Gate xor_2, 16 bits wide
  MUX_4_1x16 mux_4_1x16_1 (
    .x0(adder_1_out), .z({N, S[14:0]}), .x1(xor_2_out), .x2(B), .x3(adder_1_out), .s1(T[1]), .s0(T[0]));
  not not_1 (not_1_out, N);
  not not_2 (not_2_out, A[15]);
  not not_3 (not_3_out, B15);
  and and_1 (and_1_out, A[15], B15, not_1_out);
  and and_2 (and_2_out, not_2_out, not_3_out, N);
  or or_1 (V, and_1_out, and_2_out);
  nor nor_1 (Z, S[0], S[1], S[2], S[3], S[4], S[5], S[6], S[7], S[8], S[9], S[10], S[11], S[12], S[13], S[14], N);

  assign S[15] = N;

  // Other names for the same wires on the sheet: S15 = N
endmodule

module MUX4_1 (
  input  s1,
  input  s0,
  input  x3,
  input  x2,
  input  x1,
  input  x0,
  output z
);

  wire and_1_out, and_2_out, and_3_out, and_4_out, not_1_out, not_2_out;

  not not_1 (not_1_out, s0);
  not not_2 (not_2_out, s1);
  and and_1 (and_1_out, s1, s0, x3);
  and and_2 (and_2_out, s1, not_1_out, x2);
  and and_3 (and_3_out, s0, not_2_out, x1);
  and and_4 (and_4_out, not_1_out, not_2_out, x0);
  or or_1 (z, and_1_out, and_2_out, and_3_out, and_4_out);
endmodule

module MUX_4_1x4 (
  input  s1,
  input  s0,
  input  [3:0] x3,
  input  [3:0] x2,
  input  [3:0] x1,
  input  [3:0] x0,
  output [3:0] z
);

  MUX4_1 mux4_1_1 (.s1(s1), .s0(s0), .x3(x3[0]), .x2(x2[0]), .x1(x1[0]), .x0(x0[0]), .z(z[0]));
  MUX4_1 mux4_1_2 (.s1(s1), .s0(s0), .x3(x3[1]), .x2(x2[1]), .x1(x1[1]), .x0(x0[1]), .z(z[1]));
  MUX4_1 mux4_1_3 (.s1(s1), .s0(s0), .x3(x2[3]), .x2(x2[2]), .x1(x1[2]), .x0(x0[2]), .z(z[2]));
  MUX4_1 mux4_1_4 (.s1(s1), .s0(s0), .x3(x2[3]), .x2(x2[2]), .x1(x1[2]), .x0(x0[2]), .z(z[2]));
  MUX4_1 mux4_1_5 (.s1(s1), .s0(s0), .x3(x3[3]), .x2(x2[3]), .x1(x1[3]), .x0(x0[3]), .z(z[3]));

  // Other names for the same wires on the sheet: x0_0 = x0[0]; x1_0 = x0[1]; x2_0 = x0[2]; x3_0 = x0[3]; x0_1 = x1[0];
  //   x1_1 = x1[1]; x2_1 = x1[2]; x3_1 = x1[3]; x0_2 = x2[0]; x1_2 = x2[1]; x2_2 = x2[2]; x3_2 = x2[3]; x0_3 = x3[0];
  //   x1_3 = x3[1]; x2_3 = x3[2]; x3_3 = x3[3]
endmodule

module MUX_4_1x16 (
  input  [15:0] x0,
  input  [15:0] x1,
  input  [15:0] x2,
  input  [15:0] x3,
  input  s1,
  input  s0,
  output [15:0] z
);

  MUX_4_1x4 mux_4_1x4_1 (.s1(s1), .s0(s0), .x3(x3[3:0]), .x2(x2[3:0]), .z(z[3:0]), .x1(x1[3:0]), .x0(x0[3:0]));
  MUX_4_1x4 mux_4_1x4_2 (.s1(s1), .s0(s0), .x3(x3[7:4]), .x2(x2[7:4]), .z(z[7:4]), .x1(x1[7:4]), .x0(x0[7:4]));
  MUX_4_1x4 mux_4_1x4_3 (.s1(s1), .s0(s0), .x3(x3[11:8]), .x2(x2[11:8]), .z(z[11:8]), .x1(x1[11:8]), .x0(x0[11:8]));
  MUX_4_1x4 mux_4_1x4_4 (
    .s1(s1), .s0(s0), .x3(x3[15:12]), .x2(x2[15:12]), .z(z[15:12]), .x1(x1[15:12]), .x0(x0[15:12]));

  // Other names for the same wires on the sheet: a0[3:0] = x0[3:0]; a1[3:0] = x0[7:4]; a2[3:0] = x0[11:8];
  //   a3[3:0] = x0[15:12]; b0[3:0] = x1[3:0]; b1[3:0] = x1[7:4]; b2[3:0] = x1[11:8]; b3[3:0] = x1[15:12];
  //   c0[3:0] = x2[3:0]; c1[3:0] = x2[7:4]; c2[3:0] = x2[11:8]; c3[3:0] = x2[15:12]; d0[3:0] = x3[3:0];
  //   d1[3:0] = x3[7:4]; d2[3:0] = x3[11:8]; d3[3:0] = x3[15:12]
endmodule

module main (
);

  wire a_t, alu_1_z, and_1_out, and_2_out, and_3_out, b, clk, d_ff_1_q, FZ, fz_t, ir, nL_E, not_1_out, pc_t,
       reset;
  wire [1:0] alu, CO, mux;
  wire [3:0] estado, rom_1_data;
  wire [6:0] A, adder_1_out, D, D6_0, F, PC;
  wire [15:0] A_q, B_q, ram_1_data;
  wire [15:7] alu_1_s;

  Register #(.width(4)) u_estado (.D(rom_1_data), .Q(estado), .clk(clk), .clr(reset));  // open: en
  Register #(.width(7)) u_PC (.D(adder_1_out), .en(pc_t), .Q(PC), .clk(clk), .clr(reset));
  Register #(.width(16)) u_IR (.D(ram_1_data), .en(ir), .Q({CO, F, D}), .clk(clk));  // open: clr
  Multiplexer #(.select(2), .width(7), .enable("false")) multiplexer_1 (
    .in0(PC), .in2(F), .in3(D), .out(A), .sel(mux));  // open: in1
  ROM #(.addrWidth(7), .dataWidth(4)) rom_1 (.addr({estado, CO, FZ}), .data(rom_1_data));  // open: sel
  ROM #(.addrWidth(4), .dataWidth(10)) rom_2 (
    .addr(estado), .data({mux, alu, nL_E, pc_t, ir, a_t, b, fz_t}));  // open: sel
  Adder #(.width(7)) adder_1 (.a(7'b0000001), .b(A), .out(adder_1_out));  // open: cin, cout
  Register #(.width(16)) u_A (.D(ram_1_data), .en(a_t), .Q(A_q), .clk(clk));  // open: clr
  Register #(.width(1)) u_FZ (.D(alu_1_z), .en(fz_t), .Q(FZ), .clk(clk));  // open: clr
  ALU alu_1 (.Z(alu_1_z), .S({alu_1_s, D6_0}), .A(A_q), .B(B_q), .T(alu));  // open: V, C, N
  // Probe on CO
  // Probe on PC
  Register #(.width(16)) u_B (.D(ram_1_data), .en(b), .Q(B_q), .clk(clk));  // open: clr
  Button button_1 (.out(reset));
  Clock clock_1 (.out(clk));
  // Probe on F
  // Probe on D
  and and_1 (and_1_out, A[0], A[1], A[2], A[3], A[4], A[5], A[6], nL_E);
  and and_2 (and_2_out, and_1_out, and_3_out);
  and and_3 (and_3_out, ~D6_0[0], ~D6_0[1], ~D6_0[2], ~D6_0[3], ~D6_0[4], ~D6_0[5], ~D6_0[6]);  // AND_Gate
  RAM #(.addrWidth(7), .dataWidth(16), .bus("separate")) ram_1 (
    .addr(A), .din({alu_1_s, D6_0}), .data(ram_1_data), .str(nL_E), .sel(1'b1), .clk(clk), .ld(not_1_out));  // open: clr
  not not_1 (not_1_out, nL_E);
  // Probe on estado
  TTY tty_1 (.data(D6_0), .clk(clk), .we(and_1_out), .clr(d_ff_1_q));
  D_Flip_Flop d_ff_1 (.clk(clk), .D(and_2_out), .Q(d_ff_1_q), .en(1'b1));  // open: Qn, preset, reset

  // Notes on the sheet:
  //   Unidad de Control (cableada 12 estados)
  //   Unidad de Proceso (ruta de datos)
  //   contents of rom_1 (hex, n*v repeats v):
  //   8*1 2 2 3 3 4 4 5 5 8*6 8*8 8*a 0 b 0 b 0 b 0 b 8*7 8*0 8*9 16*0 8*1
  //   contents of rom_2 (hex, n*v repeats v):
  //   18 0 202 202 202 0 304 321 304 41 3a1 318
  //   Control de simulación
  //   0 ADD
  //   1 CMP
  //   2 MOV
  //   3 BEQ
endmodule
