// Logisim project 816106-BR32test.circ as structural Verilog: 3 circuits, main circuit BR32
module BR4 (
  input  reset,
  input  clk,
  input  [31:0] busW,
  input  [1:0] RA,
  input  [1:0] RB,
  input  [1:0] RW,
  input  RegWr,
  output [31:0] busA,
  output [31:0] busB
);

  wire decoder_1_out0, decoder_1_out1, decoder_1_out2, decoder_1_out3;
  wire [31:0] Reg1, Reg2, Reg3, Reg4;

  Decoder #(.select(2), .disabled(0)) decoder_1 (
    .out0(decoder_1_out0), .out1(decoder_1_out1), .out2(decoder_1_out2), .out3(decoder_1_out3), .sel(RW),
    .en(RegWr));
  Register #(.width(32)) Registro_1 (.D(busW), .en(decoder_1_out0), .Q(Reg1), .clk(clk), .clr(reset));
  Register #(.width(32)) Registro_2 (.D(busW), .en(decoder_1_out1), .Q(Reg2), .clk(clk), .clr(reset));
  Register #(.width(32)) Registro_3 (.D(busW), .en(decoder_1_out2), .Q(Reg3), .clk(clk), .clr(reset));
  Register #(.width(32)) Registro_4 (.D(busW), .en(decoder_1_out3), .Q(Reg4), .clk(clk), .clr(reset));
  Multiplexer #(.select(2), .width(32), .enable("false")) multiplexer_1 (
    .in0(Reg1), .in1(Reg2), .in2(Reg3), .in3(Reg4), .out(busA), .sel(RA));
  Multiplexer #(.select(2), .width(32), .enable("false")) multiplexer_2 (
    .in0(Reg1), .in1(Reg2), .in2(Reg3), .in3(Reg4), .out(busB), .sel(RB));
endmodule

module BR32 (
  input  reset,
  input  clk,
  input  [31:0] busW,
  input  [4:0] RA,
  input  [4:0] RB,
  input  [4:0] RW,
  input  RegWr,
  output [31:0] busA,
  output [31:0] busB
);

  wire Decod1, Decod2, Decod3, Decod4, Decod5, Decod6, Decod7, Decod8;
  wire [31:0] busA_1, busA_2, busA_3, busA_4, busA_5, busA_6, busA_7, busA_8, busB_1, busB_2, busB_3, busB_4,
       busB_5, busB_6, busB_7, busB_8;

  Decoder #(.select(3), .disabled(0)) decoder_1 (
    .out0(Decod1), .out1(Decod2), .out2(Decod3), .out3(Decod4), .out4(Decod5), .out5(Decod6), .out6(Decod7),
    .out7(Decod8), .sel(RW[4:2]), .en(RegWr));
  BR4 BR4_1 (
    .busW(busW), .RA(RA[1:0]), .RB(RB[1:0]), .RW(RW[1:0]), .RegWr(Decod1), .busA(busA_1), .busB(busB_1),
    .reset(reset), .clk(clk));
  BR4 BR4_3 (
    .busW(busW), .RA(RA[1:0]), .RB(RB[1:0]), .RW(RW[1:0]), .RegWr(Decod3), .busA(busA_3), .busB(busB_3),
    .reset(reset), .clk(clk));
  BR4 BR4_5 (
    .busW(busW), .RA(RA[1:0]), .RB(RB[1:0]), .RW(RW[1:0]), .RegWr(Decod5), .busA(busA_5), .busB(busB_5),
    .reset(reset), .clk(clk));
  BR4 BR4_7 (
    .busW(busW), .RA(RA[1:0]), .RB(RB[1:0]), .RW(RW[1:0]), .RegWr(Decod7), .busA(busA_7), .busB(busB_7),
    .reset(reset), .clk(clk));
  Multiplexer #(.select(3), .width(32), .enable("false")) multiplexer_1 (
    .in0(busA_1), .in1(busA_2), .in2(busA_3), .in3(busA_4), .in4(busA_5), .in5(busA_6), .in6(busA_7),
    .in7(busA_8), .out(busA), .sel(RA[4:2]));
  BR4 BR4_2 (
    .busW(busW), .RA(RA[1:0]), .RB(RB[1:0]), .RW(RW[1:0]), .RegWr(Decod2), .busA(busA_2), .busB(busB_2),
    .reset(reset), .clk(clk));
  BR4 BR4_4 (
    .busW(busW), .RA(RA[1:0]), .RB(RB[1:0]), .RW(RW[1:0]), .RegWr(Decod4), .busA(busA_4), .busB(busB_4),
    .reset(reset), .clk(clk));
  BR4 BR4_6 (
    .busW(busW), .RA(RA[1:0]), .RB(RB[1:0]), .RW(RW[1:0]), .RegWr(Decod6), .busA(busA_6), .busB(busB_6),
    .reset(reset), .clk(clk));
  BR4 BR4_8 (
    .busW(busW), .RA(RA[1:0]), .RB(RB[1:0]), .RW(RW[1:0]), .RegWr(Decod8), .busA(busA_8), .busB(busB_8),
    .reset(reset), .clk(clk));
  Multiplexer #(.select(3), .width(32), .enable("false")) multiplexer_2 (
    .in0(busB_1), .in1(busB_2), .in2(busB_3), .in3(busB_4), .in4(busB_5), .in5(busB_6), .in6(busB_7),
    .in7(busB_8), .out(busB), .sel(RB[4:2]));

  // Other names for the same wires on the sheet: RA_BR4[1:0] = RA[1:0]; RA_MUX[2:0] = RA[4:2]; RB_BR4[1:0] = RB[1:0];
  //   RB_MUX[2:0] = RB[4:2]; RW_BR4[1:0] = RW[1:0]; RW_decode[2:0] = RW[4:2]
endmodule

module main (
  output OK,
  output NO_OK
);

  wire clk, RegWr, reset;
  wire [4:0] RA, RB, RW;
  wire [6:0] br32test_1_ciclo;
  wire [31:0] busA, busB, busW;

  Clock u_clk (.out(clk));
  Button u_reset (.out(reset));
  BR32 BR32 (.reset(reset), .clk(clk), .busW(busW), .RA(RA), .RB(RB), .RW(RW), .RegWr(RegWr), .busA(busA), .busB(busB));
  BR32test br32test_1 (
    .clk(clk), .reset(reset), .busA(busA), .busB(busB), .RegWr(RegWr), .OK(OK), .busW(busW), .RW(RW),
    .RA(RA), .NO_OK(NO_OK), .RB(RB), .ciclo(br32test_1_ciclo));
  // Probe on br32test_1_ciclo
endmodule
