// Logisim project BR32test.circ as structural Verilog: 1 circuit, main circuit BR32test
module BR32test (
  input  clk,
  input  reset,
  input  [31:0] busA,
  input  [31:0] busB,
  output [6:0] ciclo,
  output RegWr,
  output OK,
  output [31:0] busW,
  output [4:0] RW,
  output [4:0] RA,
  output NO_OK,
  output [4:0] RB
);

  wire comparator_1_eq, not_1_out, or_1_out, or_2_out;
  wire [31:0] rom_5_data, rom_7_data, xor_1_out, xor_2_out;

  Counter #(.width(7), .max('h60), .ongoal("stay")) counter_1 (
    .count(not_1_out), .Q(ciclo), .clk(clk), .clr(reset));  // open: load, D, carry
  ROM #(.addrWidth(7), .dataWidth(1)) rom_1 (.addr(ciclo), .data(RegWr));  // open: sel
  ROM #(.addrWidth(7), .dataWidth(32)) rom_2 (.addr(ciclo), .data(busW));  // open: sel
  ROM #(.addrWidth(7), .dataWidth(5)) rom_3 (.addr(ciclo), .data(RW));  // open: sel
  ROM #(.addrWidth(7), .dataWidth(5)) rom_4 (.addr(ciclo), .data(RA));  // open: sel
  ROM #(.addrWidth(7), .dataWidth(32)) rom_5 (.addr(ciclo), .data(rom_5_data));  // open: sel
  ROM #(.addrWidth(7), .dataWidth(5)) rom_6 (.addr(ciclo), .data(RB));  // open: sel
  ROM #(.addrWidth(7), .dataWidth(32)) rom_7 (.addr(ciclo), .data(rom_7_data));  // open: sel
  assign xor_1_out = rom_5_data ^ busA;  // XOR_Gate xor_1, 32 bits wide
  assign xor_2_out = rom_7_data ^ busB;  // XOR_Gate xor_2, 32 bits wide
  // Probe on ciclo
  Comparator #(.width(7)) comparator_1 (.a(ciclo), .b(7'b1100000), .eq(comparator_1_eq));  // open: gt, lt
  not not_1 (not_1_out, NO_OK);
  and and_1 (OK, comparator_1_eq, not_1_out);
  or or_1 (or_1_out, xor_1_out[0], xor_1_out[1], xor_1_out[2], xor_1_out[3], xor_1_out[4], xor_1_out[5], xor_1_out[6], xor_1_out[7], xor_1_out[8], xor_1_out[9], xor_1_out[10], xor_1_out[11], xor_1_out[12], xor_1_out[13], xor_1_out[14], xor_1_out[15], xor_1_out[17], xor_1_out[18], xor_1_out[19], xor_1_out[20], xor_1_out[21], xor_1_out[22], xor_1_out[23], xor_1_out[24], xor_1_out[25], xor_1_out[26], xor_1_out[27], xor_1_out[28], xor_1_out[29], xor_1_out[30], xor_1_out[31], xor_1_out[16]);
  or or_2 (or_2_out, xor_2_out[0], xor_2_out[1], xor_2_out[2], xor_2_out[3], xor_2_out[4], xor_2_out[5], xor_2_out[6], xor_2_out[7], xor_2_out[8], xor_2_out[9], xor_2_out[10], xor_2_out[11], xor_2_out[12], xor_2_out[13], xor_2_out[14], xor_2_out[15], xor_2_out[17], xor_2_out[18], xor_2_out[19], xor_2_out[20], xor_2_out[21], xor_2_out[22], xor_2_out[23], xor_2_out[24], xor_2_out[25], xor_2_out[26], xor_2_out[27], xor_2_out[28], xor_2_out[29], xor_2_out[30], xor_2_out[31], xor_2_out[16]);
  or or_3 (NO_OK, or_1_out, or_2_out);

  // Notes on the sheet:
  //   Versión 1.1 - 2/3/2023
  //   -ciclos 65-96: RB 31 downto 0
  //   contents of rom_1 (hex, n*v repeats v):
  //   33*0 32*1
  //   contents of rom_2 (hex, n*v repeats v):
  //   34*1 2 3 4 5 6 7 8 9 a b c d e f 10 11 12 13 14 15 16 17 18 19 1a 1b 1c 1d 1e 1f 20
  //   contents of rom_3 (hex, n*v repeats v):
  //   0 1 2 3 4 5 6 7 8 9 a b c d e f 10 11 12 13 14 15 16 17 18 19 1a 1b 1c 1d 1e 1f 1f 0 1 2 3 4 5 6 7 8
  //   9 a b c d e f 10 11 12 13 14 15 16 17 18 19 1a 1b 1c 1d 1e 1f
  //   contents of rom_4 (hex, n*v repeats v):
  //   0 0 1 2 3 4 5 6 7 8 9 a b c d e f 10 11 12 13 14 15 16 17 18 19 1a 1b 1c 1d 1e 1f 33*0 1 2 3 4 5 6 7
  //   8 9 a b c d e f 10 11 12 13 14 15 16 17 18 19 1a 1b 1c 1d 1e 1f
  //   contents of rom_5 (hex, n*v repeats v):
  //   34*0 32*1 2 3 4 5 6 7 8 9 a b c d e f 10 11 12 13 14 15 16 17 18 19 1a 1b 1c 1d 1e 1f 20
  //   contents of rom_6 (hex, n*v repeats v):
  //   0 0 1 2 3 4 5 6 7 8 9 a b c d e f 10 11 12 13 14 15 16 17 18 19 1a 1b 1c 1d 1e 1f 32*0 1f 1e 1d 1c
  //   1b 1a 19 18 17 16 15 14 13 12 11 10 f e d c b a 9 8 7 6 5 4 3 2 1
  //   contents of rom_7 (hex, n*v repeats v):
  //   34*0 31*1 20 1f 1e 1d 1c 1b 1a 19 18 17 16 15 14 13 12 11 10 f e d c b a 9 8 7 6 5 4 3 2 1
endmodule
