// Logisim project MP.circ as structural Verilog: 1 circuit, main circuit main
module main (
  input  [15:0] dir,
  input  mem_en,
  input  clk,
  input  reset,
  output [31:0] dato
);

  wire en0, en1, en2, en3, ld1, ld2, not_1_out, or_1_out;
  wire [3:0] counter_1_q;
  wire [31:0] controlled_buffer_1_out, register_1_q, register_2_q, register_3_q, register_4_q, rom_1_data,
       rom_2_data, rom_3_data, rom_4_data;

  not not_1 (not_1_out, mem_en);
  Counter #(.width(4), .max('ha)) counter_1 (
    .count(mem_en), .Q(counter_1_q), .clk(clk), .clr(or_1_out));  // open: load, D, carry
  or or_1 (or_1_out, not_1_out, reset);
  Decoder #(.select(4), .disabled(0), .enable("false")) decoder_1 (
    .out2(ld1), .out3(en0), .out5(en1), .out7(en2), .out9(en3), .sel(counter_1_q));  // open: out0, out1, out4, out6, out8, out10, out11, out12, out13, out14, out15
  Register #(.width(32)) register_1 (.D(rom_1_data), .en(ld1), .Q(register_1_q), .clk(clk), .clr(reset));
  ROM #(.addrWidth(12), .dataWidth(32)) rom_1 (.addr(dir[15:4]), .data(rom_1_data));  // open: sel
  Register #(.width(32)) register_2 (.D(rom_2_data), .en(ld1), .Q(register_2_q), .clk(clk), .clr(reset));
  ROM #(.addrWidth(12), .dataWidth(32)) rom_2 (.addr(dir[15:4]), .data(rom_2_data));  // open: sel
  Register #(.width(32)) register_3 (.D(rom_3_data), .en(ld1), .Q(register_3_q), .clk(clk), .clr(reset));
  ROM #(.addrWidth(12), .dataWidth(32)) rom_3 (.addr(dir[15:4]), .data(rom_3_data));  // open: sel
  Register #(.width(32)) register_4 (.D(rom_4_data), .en(ld1), .Q(register_4_q), .clk(clk), .clr(reset));
  ROM #(.addrWidth(12), .dataWidth(32)) rom_4 (.addr(dir[15:4]), .data(rom_4_data));  // open: sel
  assign controlled_buffer_1_out = en0 ? register_1_q : 32'bz;  // Controlled_Buffer controlled_buffer_1
  assign controlled_buffer_1_out = en1 ? register_2_q : 32'bz;  // Controlled_Buffer controlled_buffer_2
  assign controlled_buffer_1_out = en2 ? register_3_q : 32'bz;  // Controlled_Buffer controlled_buffer_3
  assign controlled_buffer_1_out = en3 ? register_4_q : 32'bz;  // Controlled_Buffer controlled_buffer_4
  or or_2 (ld2, en0, en1, en2, en3);
  Register #(.width(32)) register_5 (.D(controlled_buffer_1_out), .en(ld2), .Q(dato), .clk(clk), .clr(reset));

  // Notes on the sheet:
  //   Unidad de Control
  //   contents of rom_1 (hex, n*v repeats v):
  //   0 10 20 30 40 50 60 70 80 90 a0 b0 c0 d0 e0 f0 100 110 120 130 140 150 160 170 180 190 1a0 1b0 1c0
  //   1d0 1e0 1f0 200 210 220 230 240 250 260 270 280 290 2a0 2b0 2c0 2d0 2e0 2f0 300 310 320 330 340 350
  //   360 370 380 390 3a0 3b0 3c0 3d0 3e0 3f0 400 410 420 430 440 450 460 470 480 490 4a0 4b0 4c0 4d0 4e0
  //   4f0 500 510 520 530 540 550 560 570 580 590 5a0 5b0 5c0 5d0 5e0 5f0 600 610 620 630 640 650 660 670
  //   680 690 6a0 6b0 6c0 6d0 6e0 6f0 700 710 720 730 740 750 760 770 780 790 7a0 7b0 7c0 7d0 7e0 7f0 800
  //   810 820 830 840 850 860 870 880 890 8a0 8b0 8c0 8d0 8e0 8f0 900 910 920 930 940 950 960 970 980 990
  //   9a0 9b0 9c0 9d0 9e0 9f0 a00 a10 a20 a30 a40 a50 a60 a70 a80 a90 aa0 ab0 ac0 ad0 ae0 af0 b00 b10 b20
  //   b30 b40 b50 b60 b70 b80 b90 ba0 bb0 bc0 bd0 be0 bf0 c00 c10 c20 c30 c40 c50 c60 c70 c80 c90 ca0 cb0
  //   cc0 cd0 ce0 cf0 d00 d10 d20 d30 d40 d50 d60 d70 d80 d90 da0 db0 dc0 dd0 de0 df0 e00 e10 e20 e30 e40
  //   e50 e60 e70 e80 e90 ea0 eb0 ec0 ed0 ee0 ef0 f00 f10 f20 f30 f40 f50 f60 f70 f80 f90 fa0 fb0 fc0 fd0
  //   fe0 ff0 1000 1010 1020 1030 1040 1050 1060 1070 1080 1090 10a0 10b0 10c0 10d0 10e0 10f0 1100 1110
  //   1120 1130 1140 1150 1160 1170 1180 1190 11a0 11b0 11c0 11d0 11e0 11f0 1200 1210 1220 1230 1240 1250
  //   1260 1270 1280 1290 12a0 12b0 12c0 12d0 12e0 12f0 1300 1310 1320 1330 1340 1350 1360 1370 1380 1390
  //   13a0 13b0 13c0 13d0 13e0 13f0 1400 1410 1420 1430 1440 1450 1460 1470 1480 1490 14a0 14b0 14c0 14d0
  //   14e0 14f0 1500 1510 1520 1530 1540 1550 1560 1570 1580 1590 15a0 15b0 15c0 15d0 15e0 15f0 1600 1610
  //   1620 1630 1640 1650 1660 1670 1680 1690 16a0 16b0 16c0 16d0 16e0 16f0 1700 1710 1720 1730 1740 1750
  //   1760 1770 1780 1790 17a0 17b0 17c0 17d0 17e0 17f0 1800 1810 1820 1830 1840 1850 1860 1870 1880 1890
  //   18a0 18b0 18c0 18d0 18e0 18f0 1900 1910 1920 1930 1940 1950 1960 1970 1980 1990 19a0 19b0 19c0 19d0
  //   19e0 19f0 1a00 1a10 1a20 1a30 1a40 1a50 1a60 1a70 1a80 1a90 1aa0 1ab0 1ac0 1ad0 1ae0 1af0 1b00 1b10
  //   1b20 1b30 1b40 1b50 1b60 1b70 1b80 1b90 1ba0 1bb0 1bc0 1bd0 1be0 1bf0 1c00 1c10 1c20 1c30 1c40 1c50
  //   1c60 1c70 1c80 1c90 1ca0 1cb0 1cc0 1cd0 1ce0 1cf0 1d00 1d10 1d20 1d30 1d40 1d50 1d60 1d70 1d80 1d90
  //   1da0 1db0 1dc0 1dd0 1de0 1df0 1e00 1e10 1e20 1e30 1e40 1e50 1e60 1e70 1e80 1e90 1ea0 1eb0 1ec0 1ed0
  //   1ee0 1ef0 1f00 1f10 1f20 1f30 1f40 1f50 1f60 1f70 1f80 1f90 1fa0 1fb0 1fc0 1fd0 1fe0 1ff0 2000 2010
  //   2020 2030 2040 2050 2060 2070 2080 2090 20a0 20b0 20c0 20d0 20e0 20f0 2100 2110 2120 2130 2140 2150
  //   2160 2170 2180 2190 21a0 21b0 21c0 21d0 21e0 21f0 2200 2210 2220 2230 2240 2250 2260 2270 2280 2290
  //   22a0 22b0 22c0 22d0 22e0 22f0 2300 2310 2320 2330 2340 2350 2360 2370 2380 2390 23a0 23b0 23c0 23d0
  //   23e0 23f0 2400 2410 2420 2430 2440 2450 2460 2470 2480 2490 24a0 24b0 24c0 24d0 24e0 24f0 2500 2510
  //   2520 2530 2540 2550 2560 2570 2580 2590 25a0 25b0 25c0 25d0 25e0 25f0 2600 2610 2620 2630 2640 2650
  //   2660 2670 2680 2690 26a0 26b0 26c0 26d0 26e0 26f0 2700 2710 2720 2730 2740 2750 2760 2770 2780 2790
  //   27a0 27b0 27c0 27d0 27e0 27f0 2800 2810 2820 2830 2840 2850 2860 2870 2880 2890 28a0 28b0 28c0 28d0
  //   28e0 28f0 2900 2910 2920 2930 2940 2950 2960 2970 2980 2990 29a0 29b0 29c0 29d0 29e0 29f0 2a00 2a10
  //   2a20 2a30 2a40 2a50 2a60 2a70 2a80 2a90 2aa0 2ab0 2ac0 2ad0 2ae0 2af0 2b00 2b10 2b20 2b30 2b40 2b50
  //   2b60 2b70 2b80 2b90 2ba0 2bb0 2bc0 2bd0 2be0 2bf0 2c00 2c10 2c20 2c30 2c40 2c50 2c60 2c70 2c80 2c90
  //   2ca0 2cb0 2cc0 2cd0 2ce0 2cf0 2d00 2d10 2d20 2d30 2d40 2d50 2d60 2d70 2d80 2d90 2da0 2db0 2dc0 2dd0
  //   2de0 2df0 2e00 2e10 2e20 2e30 2e40 2e50 2e60 2e70 2e80 2e90 2ea0 2eb0 2ec0 2ed0 2ee0 2ef0 2f00 2f10
  //   2f20 2f30 2f40 2f50 2f60 2f70 2f80 2f90 2fa0 2fb0 2fc0 2fd0 2fe0 2ff0 3000 3010 3020 3030 3040 3050
  //   3060 3070 3080 3090 30a0 30b0 30c0 30d0 30e0 30f0 3100 3110 3120 3130 3140 3150 3160 3170 3180 3190
  //   31a0 31b0 31c0 31d0 31e0 31f0 3200 3210 3220 3230 3240 3250 3260 3270 3280 3290 32a0 32b0 32c0 32d0
  //   32e0 32f0 3300 3310 3320 3330 3340 3350 3360 3370 3380 3390 33a0 33b0 33c0 33d0 33e0 33f0 3400 3410
  //   3420 3430 3440 3450 3460 3470 3480 3490 34a0 34b0 34c0 34d0 34e0 34f0 3500 3510 3520 3530 3540 3550
  //   356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
  //   contents of rom_2 (hex, n*v repeats v):
  //   4 14 24 34 44 54 64 74 84 94 a4 b4 c4 d4 e4 f4 104 114 124 134 144 154 164 174 184 194 1a4 1b4 1c4
  //   1d4 1e4 1f4 204 214 224 234 244 254 264 274 284 294 2a4 2b4 2c4 2d4 2e4 2f4 304 314 324 334 344 354
  //   364 374 384 394 3a4 3b4 3c4 3d4 3e4 3f4 404 414 424 434 444 454 464 474 484 494 4a4 4b4 4c4 4d4 4e4
  //   4f4 504 514 524 534 544 554 564 574 584 594 5a4 5b4 5c4 5d4 5e4 5f4 604 614 624 634 644 654 664 674
  //   684 694 6a4 6b4 6c4 6d4 6e4 6f4 704 714 724 734 744 754 764 774 784 794 7a4 7b4 7c4 7d4 7e4 7f4 804
  //   814 824 834 844 854 864 874 884 894 8a4 8b4 8c4 8d4 8e4 8f4 904 914 924 934 944 954 964 974 984 994
  //   9a4 9b4 9c4 9d4 9e4 9f4 a04 a14 a24 a34 a44 a54 a64 a74 a84 a94 aa4 ab4 ac4 ad4 ae4 af4 b04 b14 b24
  //   b34 b44 b54 b64 b74 b84 b94 ba4 bb4 bc4 bd4 be4 bf4 c04 c14 c24 c34 c44 c54 c64 c74 c84 c94 ca4 cb4
  //   cc4 cd4 ce4 cf4 d04 d14 d24 d34 d44 d54 d64 d74 d84 d94 da4 db4 dc4 dd4 de4 df4 e04 e14 e24 e34 e44
  //   e54 e64 e74 e84 e94 ea4 eb4 ec4 ed4 ee4 ef4 f04 f14 f24 f34 f44 f54 f64 f74 f84 f94 fa4 fb4 fc4 fd4
  //   fe4 ff4 1004 1014 1024 1034 1044 1054 1064 1074 1084 1094 10a4 10b4 10c4 10d4 10e4 10f4 1104 1114
  //   1124 1134 1144 1154 1164 1174 1184 1194 11a4 11b4 11c4 11d4 11e4 11f4 1204 1214 1224 1234 1244 1254
  //   1264 1274 1284 1294 12a4 12b4 12c4 12d4 12e4 12f4 1304 1314 1324 1334 1344 1354 1364 1374 1384 1394
  //   13a4 13b4 13c4 13d4 13e4 13f4 1404 1414 1424 1434 1444 1454 1464 1474 1484 1494 14a4 14b4 14c4 14d4
  //   14e4 14f4 1504 1514 1524 1534 1544 1554 1564 1574 1584 1594 15a4 15b4 15c4 15d4 15e4 15f4 1604 1614
  //   1624 1634 1644 1654 1664 1674 1684 1694 16a4 16b4 16c4 16d4 16e4 16f4 1704 1714 1724 1734 1744 1754
  //   1764 1774 1784 1794 17a4 17b4 17c4 17d4 17e4 17f4 1804 1814 1824 1834 1844 1854 1864 1874 1884 1894
  //   18a4 18b4 18c4 18d4 18e4 18f4 1904 1914 1924 1934 1944 1954 1964 1974 1984 1994 19a4 19b4 19c4 19d4
  //   19e4 19f4 1a04 1a14 1a24 1a34 1a44 1a54 1a64 1a74 1a84 1a94 1aa4 1ab4 1ac4 1ad4 1ae4 1af4 1b04 1b14
  //   1b24 1b34 1b44 1b54 1b64 1b74 1b84 1b94 1ba4 1bb4 1bc4 1bd4 1be4 1bf4 1c04 1c14 1c24 1c34 1c44 1c54
  //   1c64 1c74 1c84 1c94 1ca4 1cb4 1cc4 1cd4 1ce4 1cf4 1d04 1d14 1d24 1d34 1d44 1d54 1d64 1d74 1d84 1d94
  //   1da4 1db4 1dc4 1dd4 1de4 1df4 1e04 1e14 1e24 1e34 1e44 1e54 1e64 1e74 1e84 1e94 1ea4 1eb4 1ec4 1ed4
  //   1ee4 1ef4 1f04 1f14 1f24 1f34 1f44 1f54 1f64 1f74 1f84 1f94 1fa4 1fb4 1fc4 1fd4 1fe4 1ff4 2004 2014
  //   2024 2034 2044 2054 2064 2074 2084 2094 20a4 20b4 20c4 20d4 20e4 20f4 2104 2114 2124 2134 2144 2154
  //   2164 2174 2184 2194 21a4 21b4 21c4 21d4 21e4 21f4 2204 2214 2224 2234 2244 2254 2264 2274 2284 2294
  //   22a4 22b4 22c4 22d4 22e4 22f4 2304 2314 2324 2334 2344 2354 2364 2374 2384 2394 23a4 23b4 23c4 23d4
  //   23e4 23f4 2404 2414 2424 2434 2444 2454 2464 2474 2484 2494 24a4 24b4 24c4 24d4 24e4 24f4 2504 2514
  //   2524 2534 2544 2554 2564 2574 2584 2594 25a4 25b4 25c4 25d4 25e4 25f4 2604 2614 2624 2634 2644 2654
  //   2664 2674 2684 2694 26a4 26b4 26c4 26d4 26e4 26f4 2704 2714 2724 2734 2744 2754 2764 2774 2784 2794
  //   27a4 27b4 27c4 27d4 27e4 27f4 2804 2814 2824 2834 2844 2854 2864 2874 2884 2894 28a4 28b4 28c4 28d4
  //   28e4 28f4 2904 2914 2924 2934 2944 2954 2964 2974 2984 2994 29a4 29b4 29c4 29d4 29e4 29f4 2a04 2a14
  //   2a24 2a34 2a44 2a54 2a64 2a74 2a84 2a94 2aa4 2ab4 2ac4 2ad4 2ae4 2af4 2b04 2b14 2b24 2b34 2b44 2b54
  //   2b64 2b74 2b84 2b94 2ba4 2bb4 2bc4 2bd4 2be4 2bf4 2c04 2c14 2c24 2c34 2c44 2c54 2c64 2c74 2c84 2c94
  //   2ca4 2cb4 2cc4 2cd4 2ce4 2cf4 2d04 2d14 2d24 2d34 2d44 2d54 2d64 2d74 2d84 2d94 2da4 2db4 2dc4 2dd4
  //   2de4 2df4 2e04 2e14 2e24 2e34 2e44 2e54 2e64 2e74 2e84 2e94 2ea4 2eb4 2ec4 2ed4 2ee4 2ef4 2f04 2f14
  //   2f24 2f34 2f44 2f54 2f64 2f74 2f84 2f94 2fa4 2fb4 2fc4 2fd4 2fe4 2ff4 3004 3014 3024 3034 3044 3054
  //   3064 3074 3084 3094 30a4 30b4 30c4 30d4 30e4 30f4 3104 3114 3124 3134 3144 3154 3164 3174 3184 3194
  //   31a4 31b4 31c4 31d4 31e4 31f4 3204 3214 3224 3234 3244 3254 3264 3274 3284 3294 32a4 32b4 32c4 32d4
  //   32e4 32f4 3304 3314 3324 3334 3344 3354 3364 3374 3384 3394 33a4 33b4 33c4 33d4 33e4 33f4 3404 3414
  //   3424 3434 3444 3454 3464 3474 3484 3494 34a4 34b4 34c4 34d4 34e4 34f4 3504 3514 3524 3534 3544 3554
  //   356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
  //   contents of rom_3 (hex, n*v repeats v):
  //   8 18 28 38 48 58 68 78 88 98 a8 b8 c8 d8 e8 f8 108 118 128 138 148 158 168 178 188 198 1a8 1b8 1c8
  //   1d8 1e8 1f8 208 218 228 238 248 258 268 278 288 298 2a8 2b8 2c8 2d8 2e8 2f8 308 318 328 338 348 358
  //   368 378 388 398 3a8 3b8 3c8 3d8 3e8 3f8 408 418 428 438 448 458 468 478 488 498 4a8 4b8 4c8 4d8 4e8
  //   4f8 508 518 528 538 548 558 568 578 588 598 5a8 5b8 5c8 5d8 5e8 5f8 608 618 628 638 648 658 668 678
  //   688 698 6a8 6b8 6c8 6d8 6e8 6f8 708 718 728 738 748 758 768 778 788 798 7a8 7b8 7c8 7d8 7e8 7f8 808
  //   818 828 838 848 858 868 878 888 898 8a8 8b8 8c8 8d8 8e8 8f8 908 918 928 938 948 958 968 978 988 998
  //   9a8 9b8 9c8 9d8 9e8 9f8 a08 a18 a28 a38 a48 a58 a68 a78 a88 a98 aa8 ab8 ac8 ad8 ae8 af8 b08 b18 b28
  //   b38 b48 b58 b68 b78 b88 b98 ba8 bb8 bc8 bd8 be8 bf8 c08 c18 c28 c38 c48 c58 c68 c78 c88 c98 ca8 cb8
  //   cc8 cd8 ce8 cf8 d08 d18 d28 d38 d48 d58 d68 d78 d88 d98 da8 db8 dc8 dd8 de8 df8 e08 e18 e28 e38 e48
  //   e58 e68 e78 e88 e98 ea8 eb8 ec8 ed8 ee8 ef8 f08 f18 f28 f38 f48 f58 f68 f78 f88 f98 fa8 fb8 fc8 fd8
  //   fe8 ff8 1008 1018 1028 1038 1048 1058 1068 1078 1088 1098 10a8 10b8 10c8 10d8 10e8 10f8 1108 1118
  //   1128 1138 1148 1158 1168 1178 1188 1198 11a8 11b8 11c8 11d8 11e8 11f8 1208 1218 1228 1238 1248 1258
  //   1268 1278 1288 1298 12a8 12b8 12c8 12d8 12e8 12f8 1308 1318 1328 1338 1348 1358 1368 1378 1388 1398
  //   13a8 13b8 13c8 13d8 13e8 13f8 1408 1418 1428 1438 1448 1458 1468 1478 1488 1498 14a8 14b8 14c8 14d8
  //   14e8 14f8 1508 1518 1528 1538 1548 1558 1568 1578 1588 1598 15a8 15b8 15c8 15d8 15e8 15f8 1608 1618
  //   1628 1638 1648 1658 1668 1678 1688 1698 16a8 16b8 16c8 16d8 16e8 16f8 1708 1718 1728 1738 1748 1758
  //   1768 1778 1788 1798 17a8 17b8 17c8 17d8 17e8 17f8 1808 1818 1828 1838 1848 1858 1868 1878 1888 1898
  //   18a8 18b8 18c8 18d8 18e8 18f8 1908 1918 1928 1938 1948 1958 1968 1978 1988 1998 19a8 19b8 19c8 19d8
  //   19e8 19f8 1a08 1a18 1a28 1a38 1a48 1a58 1a68 1a78 1a88 1a98 1aa8 1ab8 1ac8 1ad8 1ae8 1af8 1b08 1b18
  //   1b28 1b38 1b48 1b58 1b68 1b78 1b88 1b98 1ba8 1bb8 1bc8 1bd8 1be8 1bf8 1c08 1c18 1c28 1c38 1c48 1c58
  //   1c68 1c78 1c88 1c98 1ca8 1cb8 1cc8 1cd8 1ce8 1cf8 1d08 1d18 1d28 1d38 1d48 1d58 1d68 1d78 1d88 1d98
  //   1da8 1db8 1dc8 1dd8 1de8 1df8 1e08 1e18 1e28 1e38 1e48 1e58 1e68 1e78 1e88 1e98 1ea8 1eb8 1ec8 1ed8
  //   1ee8 1ef8 1f08 1f18 1f28 1f38 1f48 1f58 1f68 1f78 1f88 1f98 1fa8 1fb8 1fc8 1fd8 1fe8 1ff8 2008 2018
  //   2028 2038 2048 2058 2068 2078 2088 2098 20a8 20b8 20c8 20d8 20e8 20f8 2108 2118 2128 2138 2148 2158
  //   2168 2178 2188 2198 21a8 21b8 21c8 21d8 21e8 21f8 2208 2218 2228 2238 2248 2258 2268 2278 2288 2298
  //   22a8 22b8 22c8 22d8 22e8 22f8 2308 2318 2328 2338 2348 2358 2368 2378 2388 2398 23a8 23b8 23c8 23d8
  //   23e8 23f8 2408 2418 2428 2438 2448 2458 2468 2478 2488 2498 24a8 24b8 24c8 24d8 24e8 24f8 2508 2518
  //   2528 2538 2548 2558 2568 2578 2588 2598 25a8 25b8 25c8 25d8 25e8 25f8 2608 2618 2628 2638 2648 2658
  //   2668 2678 2688 2698 26a8 26b8 26c8 26d8 26e8 26f8 2708 2718 2728 2738 2748 2758 2768 2778 2788 2798
  //   27a8 27b8 27c8 27d8 27e8 27f8 2808 2818 2828 2838 2848 2858 2868 2878 2888 2898 28a8 28b8 28c8 28d8
  //   28e8 28f8 2908 2918 2928 2938 2948 2958 2968 2978 2988 2998 29a8 29b8 29c8 29d8 29e8 29f8 2a08 2a18
  //   2a28 2a38 2a48 2a58 2a68 2a78 2a88 2a98 2aa8 2ab8 2ac8 2ad8 2ae8 2af8 2b08 2b18 2b28 2b38 2b48 2b58
  //   2b68 2b78 2b88 2b98 2ba8 2bb8 2bc8 2bd8 2be8 2bf8 2c08 2c18 2c28 2c38 2c48 2c58 2c68 2c78 2c88 2c98
  //   2ca8 2cb8 2cc8 2cd8 2ce8 2cf8 2d08 2d18 2d28 2d38 2d48 2d58 2d68 2d78 2d88 2d98 2da8 2db8 2dc8 2dd8
  //   2de8 2df8 2e08 2e18 2e28 2e38 2e48 2e58 2e68 2e78 2e88 2e98 2ea8 2eb8 2ec8 2ed8 2ee8 2ef8 2f08 2f18
  //   2f28 2f38 2f48 2f58 2f68 2f78 2f88 2f98 2fa8 2fb8 2fc8 2fd8 2fe8 2ff8 3008 3018 3028 3038 3048 3058
  //   3068 3078 3088 3098 30a8 30b8 30c8 30d8 30e8 30f8 3108 3118 3128 3138 3148 3158 3168 3178 3188 3198
  //   31a8 31b8 31c8 31d8 31e8 31f8 3208 3218 3228 3238 3248 3258 3268 3278 3288 3298 32a8 32b8 32c8 32d8
  //   32e8 32f8 3308 3318 3328 3338 3348 3358 3368 3378 3388 3398 33a8 33b8 33c8 33d8 33e8 33f8 3408 3418
  //   3428 3438 3448 3458 3468 3478 3488 3498 34a8 34b8 34c8 34d8 34e8 34f8 3508 3518 3528 3538 3548 3558
  //   356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
  //   contents of rom_4 (hex, n*v repeats v):
  //   c 1c 2c 3c 4c 5c 6c 7c 8c 9c ac bc cc dc ec fc 10c 11c 12c 13c 14c 15c 16c 17c 18c 19c 1ac 1bc 1cc
  //   1dc 1ec 1fc 20c 21c 22c 23c 24c 25c 26c 27c 28c 29c 2ac 2bc 2cc 2dc 2ec 2fc 30c 31c 32c 33c 34c 35c
  //   36c 37c 38c 39c 3ac 3bc 3cc 3dc 3ec 3fc 40c 41c 42c 43c 44c 45c 46c 47c 48c 49c 4ac 4bc 4cc 4dc 4ec
  //   4fc 50c 51c 52c 53c 54c 55c 56c 57c 58c 59c 5ac 5bc 5cc 5dc 5ec 5fc 60c 61c 62c 63c 64c 65c 66c 67c
  //   68c 69c 6ac 6bc 6cc 6dc 6ec 6fc 70c 71c 72c 73c 74c 75c 76c 77c 78c 79c 7ac 7bc 7cc 7dc 7ec 7fc 80c
  //   81c 82c 83c 84c 85c 86c 87c 88c 89c 8ac 8bc 8cc 8dc 8ec 8fc 90c 91c 92c 93c 94c 95c 96c 97c 98c 99c
  //   9ac 9bc 9cc 9dc 9ec 9fc a0c a1c a2c a3c a4c a5c a6c a7c a8c a9c aac abc acc adc aec afc b0c b1c b2c
  //   b3c b4c b5c b6c b7c b8c b9c bac bbc bcc bdc bec bfc c0c c1c c2c c3c c4c c5c c6c c7c c8c c9c cac cbc
  //   ccc cdc cec cfc d0c d1c d2c d3c d4c d5c d6c d7c d8c d9c dac dbc dcc ddc dec dfc e0c e1c e2c e3c e4c
  //   e5c e6c e7c e8c e9c eac ebc ecc edc eec efc f0c f1c f2c f3c f4c f5c f6c f7c f8c f9c fac fbc fcc fdc
  //   fec ffc 100c 101c 102c 103c 104c 105c 106c 107c 108c 109c 10ac 10bc 10cc 10dc 10ec 10fc 110c 111c
  //   112c 113c 114c 115c 116c 117c 118c 119c 11ac 11bc 11cc 11dc 11ec 11fc 120c 121c 122c 123c 124c 125c
  //   126c 127c 128c 129c 12ac 12bc 12cc 12dc 12ec 12fc 130c 131c 132c 133c 134c 135c 136c 137c 138c 139c
  //   13ac 13bc 13cc 13dc 13ec 13fc 140c 141c 142c 143c 144c 145c 146c 147c 148c 149c 14ac 14bc 14cc 14dc
  //   14ec 14fc 150c 151c 152c 153c 154c 155c 156c 157c 158c 159c 15ac 15bc 15cc 15dc 15ec 15fc 160c 161c
  //   162c 163c 164c 165c 166c 167c 168c 169c 16ac 16bc 16cc 16dc 16ec 16fc 170c 171c 172c 173c 174c 175c
  //   176c 177c 178c 179c 17ac 17bc 17cc 17dc 17ec 17fc 180c 181c 182c 183c 184c 185c 186c 187c 188c 189c
  //   18ac 18bc 18cc 18dc 18ec 18fc 190c 191c 192c 193c 194c 195c 196c 197c 198c 199c 19ac 19bc 19cc 19dc
  //   19ec 19fc 1a0c 1a1c 1a2c 1a3c 1a4c 1a5c 1a6c 1a7c 1a8c 1a9c 1aac 1abc 1acc 1adc 1aec 1afc 1b0c 1b1c
  //   1b2c 1b3c 1b4c 1b5c 1b6c 1b7c 1b8c 1b9c 1bac 1bbc 1bcc 1bdc 1bec 1bfc 1c0c 1c1c 1c2c 1c3c 1c4c 1c5c
  //   1c6c 1c7c 1c8c 1c9c 1cac 1cbc 1ccc 1cdc 1cec 1cfc 1d0c 1d1c 1d2c 1d3c 1d4c 1d5c 1d6c 1d7c 1d8c 1d9c
  //   1dac 1dbc 1dcc 1ddc 1dec 1dfc 1e0c 1e1c 1e2c 1e3c 1e4c 1e5c 1e6c 1e7c 1e8c 1e9c 1eac 1ebc 1ecc 1edc
  //   1eec 1efc 1f0c 1f1c 1f2c 1f3c 1f4c 1f5c 1f6c 1f7c 1f8c 1f9c 1fac 1fbc 1fcc 1fdc 1fec 1ffc 200c 201c
  //   202c 203c 204c 205c 206c 207c 208c 209c 20ac 20bc 20cc 20dc 20ec 20fc 210c 211c 212c 213c 214c 215c
  //   216c 217c 218c 219c 21ac 21bc 21cc 21dc 21ec 21fc 220c 221c 222c 223c 224c 225c 226c 227c 228c 229c
  //   22ac 22bc 22cc 22dc 22ec 22fc 230c 231c 232c 233c 234c 235c 236c 237c 238c 239c 23ac 23bc 23cc 23dc
  //   23ec 23fc 240c 241c 242c 243c 244c 245c 246c 247c 248c 249c 24ac 24bc 24cc 24dc 24ec 24fc 250c 251c
  //   252c 253c 254c 255c 256c 257c 258c 259c 25ac 25bc 25cc 25dc 25ec 25fc 260c 261c 262c 263c 264c 265c
  //   266c 267c 268c 269c 26ac 26bc 26cc 26dc 26ec 26fc 270c 271c 272c 273c 274c 275c 276c 277c 278c 279c
  //   27ac 27bc 27cc 27dc 27ec 27fc 280c 281c 282c 283c 284c 285c 286c 287c 288c 289c 28ac 28bc 28cc 28dc
  //   28ec 28fc 290c 291c 292c 293c 294c 295c 296c 297c 298c 299c 29ac 29bc 29cc 29dc 29ec 29fc 2a0c 2a1c
  //   2a2c 2a3c 2a4c 2a5c 2a6c 2a7c 2a8c 2a9c 2aac 2abc 2acc 2adc 2aec 2afc 2b0c 2b1c 2b2c 2b3c 2b4c 2b5c
  //   2b6c 2b7c 2b8c 2b9c 2bac 2bbc 2bcc 2bdc 2bec 2bfc 2c0c 2c1c 2c2c 2c3c 2c4c 2c5c 2c6c 2c7c 2c8c 2c9c
  //   2cac 2cbc 2ccc 2cdc 2cec 2cfc 2d0c 2d1c 2d2c 2d3c 2d4c 2d5c 2d6c 2d7c 2d8c 2d9c 2dac 2dbc 2dcc 2ddc
  //   2dec 2dfc 2e0c 2e1c 2e2c 2e3c 2e4c 2e5c 2e6c 2e7c 2e8c 2e9c 2eac 2ebc 2ecc 2edc 2eec 2efc 2f0c 2f1c
  //   2f2c 2f3c 2f4c 2f5c 2f6c 2f7c 2f8c 2f9c 2fac 2fbc 2fcc 2fdc 2fec 2ffc 300c 301c 302c 303c 304c 305c
  //   306c 307c 308c 309c 30ac 30bc 30cc 30dc 30ec 30fc 310c 311c 312c 313c 314c 315c 316c 317c 318c 319c
  //   31ac 31bc 31cc 31dc 31ec 31fc 320c 321c 322c 323c 324c 325c 326c 327c 328c 329c 32ac 32bc 32cc 32dc
  //   32ec 32fc 330c 331c 332c 333c 334c 335c 336c 337c 338c 339c 33ac 33bc 33cc 33dc 33ec 33fc 340c 341c
  //   342c 343c 344c 345c 346c 347c 348c 349c 34ac 34bc 34cc 34dc 34ec 34fc 350c 351c 352c 353c 354c 355c
  //   356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
endmodule
