// Logisim project 816106-cache.circ as structural Verilog: 1 circuit, main circuit main
// 0xd
module main (
  input  in_1
);

  wire cache_test5_1_ok, cache_write, clk, comparator_1_eq, comparator_2_eq, hit, hit_v0, hit_v1, mem_en,
       not_1_out, not_2_out, not_4_out, or_1_out, Reg_word0, Reg_word1, Reg_word2, Reg_word3, valid_v1,
       valid_v2, way_to_replace, WE_way0, WE_way1;
  wire [1:0] \byte ;
  wire [2:0] cache_test5_1_err;
  wire [3:0] cicle;
  wire [3:2] tunnel;
  wire [4:0] set;
  wire [6:0] cache_test5_1_ciclo, tag, tag_v1, tag_v2;
  wire [7:0] counter_2_q;
  wire [31:0] bus, bus_word0, bus_word1, bus_word2, bus_word3, data0_v0, data0_v1, data1_v0, data1_v1,
       data2_v0, data2_v1, data3_v0, data3_v1, data_v0, data_v1, inst;

  Clock clock_1 (.out(clk));
  // Probe on cicle
  not not_1 (not_1_out, way_to_replace);
  Comparator #(.width(7)) comparator_1 (.a(tag), .b(tag_v1), .eq(comparator_1_eq));  // open: gt, lt
  Comparator #(.width(7)) comparator_2 (.a(tag), .b(tag_v2), .eq(comparator_2_eq));  // open: gt, lt
  not not_2 (not_2_out, mem_en);
  RAM #(.addrWidth(5), .dataWidth(1), .bus("separate")) ram_1 (
    .addr(set), .din(not_1_out), .data(way_to_replace), .str(cache_write), .clk(clk), .clr(in_1));  // open: sel, ld
  Counter #(.width(4), .max('hc)) counter_1 (
    .count(mem_en), .Q(cicle), .clk(clk), .clr(or_1_out));  // open: load, D, carry
  or or_1 (or_1_out, not_2_out, in_1);
  and and_1 (hit_v0, comparator_1_eq, valid_v1);
  and and_2 (hit_v1, comparator_2_eq, valid_v2);
  Decoder #(.select(4), .disabled(0), .enable("false")) decoder_1 (
    .out4(Reg_word0), .out6(Reg_word1), .out8(Reg_word2), .out10(Reg_word3), .out11(cache_write), .sel(cicle));  // open: out0, out1, out2, out3, out5, out7, out9, out12, out13, out14, out15
  or or_2 (hit, hit_v0, hit_v1);
  MP_main MP (.dir({tag, set, tunnel, \byte }), .mem_en(mem_en), .clk(clk), .reset(in_1), .dato(bus));
  not not_3 (mem_en, hit);
  RAM #(.addrWidth(5), .bus("separate")) ram_2 (
    .addr(set), .din({tag, 1'b1}), .data({tag_v1, valid_v1}), .str(WE_way0), .clk(clk), .clr(in_1));  // open: sel, ld
  RAM #(.addrWidth(5), .bus("separate")) ram_3 (
    .addr(set), .din({tag, 1'b1}), .data({tag_v2, valid_v2}), .str(WE_way1), .clk(clk), .clr(in_1));  // open: sel, ld
  not not_4 (not_4_out, way_to_replace);
  and and_3 (WE_way0, not_4_out, cache_write);
  and and_4 (WE_way1, way_to_replace, cache_write);
  // Probe on cache_test5_1_ok
  RAM #(.addrWidth(5), .dataWidth(32), .bus("separate")) ram_4 (
    .addr(set), .din(bus_word0), .data(data0_v0), .str(WE_way0), .clk(clk), .clr(in_1));  // open: sel, ld
  RAM #(.addrWidth(5), .dataWidth(32), .bus("separate")) ram_5 (
    .addr(set), .din(bus_word2), .data(data2_v0), .str(WE_way0), .clk(clk), .clr(in_1));  // open: sel, ld
  // Probe on cache_test5_1_ciclo
  // Probe on cache_test5_1_err
  cache_test5 cache_test5_1 (
    .clk(clk), .reset(in_1), .inst(inst), .OK(cache_test5_1_ok), .in_3({tag, set, tunnel, \byte }),
    .ERR(cache_test5_1_err), .ciclo(cache_test5_1_ciclo), .hit(hit), .way(hit_v1), .set(set), .nia(20'hc73ea));
  // Probe on 20'hc73ea
  Register #(.width(32)) register_1 (.D(bus), .en(Reg_word0), .Q(bus_word0), .clk(clk), .clr(in_1));
  Register #(.width(32)) register_2 (.D(bus), .en(Reg_word1), .Q(bus_word1), .clk(clk), .clr(in_1));
  RAM #(.addrWidth(5), .dataWidth(32), .bus("separate")) ram_6 (
    .addr(set), .din(bus_word1), .data(data1_v0), .str(WE_way0), .clk(clk), .clr(in_1));  // open: sel, ld
  RAM #(.addrWidth(5), .dataWidth(32), .bus("separate")) ram_7 (
    .addr(set), .din(bus_word3), .data(data3_v0), .str(WE_way0), .clk(clk), .clr(in_1));  // open: sel, ld
  Multiplexer #(.select(2), .width(32)) multiplexer_1 (
    .in0(data0_v0), .in1(data1_v0), .in2(data2_v0), .in3(data3_v0), .out(data_v0), .sel(tunnel), .en(hit));
  Multiplexer #(.select(2), .width(32)) multiplexer_2 (
    .in0(data0_v1), .in1(data1_v1), .in2(data2_v1), .in3(data3_v1), .out(data_v1), .sel(tunnel), .en(hit));
  Counter counter_2 (.count(hit), .Q(counter_2_q), .clk(clk), .clr(in_1));  // open: load, D, carry
  Register #(.width(32)) register_3 (.D(bus), .en(Reg_word2), .Q(bus_word2), .clk(clk), .clr(in_1));
  Multiplexer #(.width(32)) multiplexer_3 (.in0(data_v0), .in1(data_v1), .out(inst), .sel(hit_v1), .en(hit));
  ROM #(.dataWidth(16)) rom_1 (.addr(counter_2_q), .data({tag, set, tunnel, \byte }));  // open: sel
  Register #(.width(32)) register_4 (.D(bus), .en(Reg_word3), .Q(bus_word3), .clk(clk), .clr(in_1));
  RAM #(.addrWidth(5), .dataWidth(32), .bus("separate")) ram_8 (
    .addr(set), .din(bus_word0), .data(data0_v1), .str(WE_way1), .clk(clk), .clr(in_1));  // open: sel, ld
  RAM #(.addrWidth(5), .dataWidth(32), .bus("separate")) ram_9 (
    .addr(set), .din(bus_word2), .data(data2_v1), .str(WE_way1), .clk(clk), .clr(in_1));  // open: sel, ld
  // Probe on inst
  RAM #(.addrWidth(5), .dataWidth(32), .bus("separate")) ram_10 (
    .addr(set), .din(bus_word1), .data(data1_v1), .str(WE_way1), .clk(clk), .clr(in_1));  // open: sel, ld
  RAM #(.addrWidth(5), .dataWidth(32), .bus("separate")) ram_11 (
    .addr(set), .din(bus_word3), .data(data3_v1), .str(WE_way1), .clk(clk), .clr(in_1));  // open: sel, ld

  // Other names for the same wires on the sheet: miss = mem_en; reset = in_1; tunnel (some bits) = {tag, set, \byte };
  //   word[1:0] = tunnel; way = hit_v1

  // Notes on the sheet:
  //   Gestión de etiquetas
  //   Unidad de control
  //   Via 0
  //   Gestión de datos
  //   contents of rom_1 (hex, n*v repeats v):
  //   200 400 600 60c 3d0 5d4 7d0 5d8 1008 1200 2204 1208
  //   Via 1
endmodule
