// Logisim project MC.circ as structural Verilog: 1 circuit, main circuit main
module main (
  output out_1
);

  wire clk, mem_en, undriven, undriven_3, valid_v1;
  wire [3:0] tunnel;
  wire [4:0] set;
  wire [6:0] tag, tag_v1;
  wire [7:0] counter_1_q, undriven_2;
  wire [31:0] bus;

  Clock clock_1 (.out(clk));
  RAM #(.addrWidth(5), .dataWidth(1)) ram_1 ();  // open: addr, data, sel, clk, ld, clr
  RAM #(.addrWidth(5)) ram_2 (.addr(set), .data({tag_v1, valid_v1}));  // open: sel, clk, ld, clr
  RAM #(.addrWidth(5)) ram_3 (.addr(set), .data({tag_v1, valid_v1}));  // open: sel, clk, ld, clr
  Register #(.width(32)) register_1 ();  // open: D, en, Q, clk, clr
  Register #(.width(32)) register_2 ();  // open: D, en, Q, clk, clr
  Register #(.width(32)) register_3 ();  // open: D, en, Q, clk, clr
  RAM #(.addrWidth(5), .dataWidth(32)) ram_4 ();  // open: addr, data, sel, clk, ld, clr
  RAM #(.addrWidth(5), .dataWidth(32)) ram_5 ();  // open: addr, data, sel, clk, ld, clr
  MP_main MP (.dir({tag, set, tunnel}), .mem_en(mem_en), .clk(clk), .reset(out_1), .dato(bus));
  Register #(.width(32)) register_4 ();  // open: D, en, Q, clk, clr
  Multiplexer #(.select(2)) multiplexer_1 ();  // open: in0, in1, in2, in3, out, sel, en
  RAM #(.addrWidth(5), .dataWidth(32)) ram_6 ();  // open: addr, data, sel, clk, ld, clr
  RAM #(.addrWidth(5), .dataWidth(32)) ram_7 ();  // open: addr, data, sel, clk, ld, clr
  Multiplexer multiplexer_2 ();  // open: in0, in1, out, sel, en
  RAM #(.addrWidth(5), .dataWidth(32)) ram_8 ();  // open: addr, data, sel, clk, ld, clr
  RAM #(.addrWidth(5), .dataWidth(32)) ram_9 ();  // open: addr, data, sel, clk, ld, clr
  Multiplexer #(.select(2)) multiplexer_3 ();  // open: in0, in1, in2, in3, out, sel, en
  Counter counter_1 (
    .load(undriven), .D(undriven_2), .count(undriven_3), .Q(counter_1_q), .clk(clk), .clr(out_1));  // open: carry
  RAM #(.addrWidth(5), .dataWidth(32)) ram_10 ();  // open: addr, data, sel, clk, ld, clr
  RAM #(.addrWidth(5), .dataWidth(32)) ram_11 ();  // open: addr, data, sel, clk, ld, clr
  ROM #(.dataWidth(16)) rom_1 (.addr(counter_1_q), .data({tag, set, tunnel}));  // open: sel

  // Other names for the same wires on the sheet: reset = out_1; word[3:0] = tunnel; tunnel[15:4] = {tag, set}
endmodule
