// Logisim project cache test5.circ as structural Verilog: 1 circuit, main circuit cache test5
module cache_test5 (
  input  clk,
  input  reset,
  input  [15:0] in_3,
  input  [31:0] inst,
  input  hit,
  input  way,
  input  [4:0] set,
  input  [19:0] nia,
  output [6:0] ciclo,
  output OK,
  output [2:0] ERR
);

  wire and_2_out, and_4_out, and_5_out, and_7_out, and_8_out, and_9_out, check, comparator_1_eq,
       comparator_2_gt, comparator_3_eq, comparator_4_eq, comparator_5_eq, comparator_6_eq, comparator_7_eq,
       count, err1, err2, err3, err4, err5, fin, multiplexer_1_out, not_2_out, or_1_out, Q0, Q0r, Q1,
       Q1_plus, Q2, rom_1_data, xnor_1_out;
  wire [1:0] rom_3_data;
  wire [2:0] priority_encoder_1_out, register_3_q, rom_2_data;
  wire [4:0] cto, multiplexer_2_out;
  wire [15:0] register_1_q, register_2_q;

  Counter #(.width(7), .max('h77), .ongoal("stay")) counter_1 (
    .count(count), .Q(ciclo), .clk(clk), .clr(reset));  // open: load, D, carry
  ROM #(.addrWidth(7), .dataWidth(1)) rom_1 (.addr(ciclo), .data(rom_1_data));  // open: sel
  ROM #(.addrWidth(7), .dataWidth(3)) rom_2 (.addr(ciclo), .data(rom_2_data));  // open: sel
  ROM #(.addrWidth(7), .dataWidth(2)) rom_3 (.addr(ciclo), .data(rom_3_data));  // open: sel
  Register #(.width(16)) register_1 (.D(in_3), .en(hit), .Q(register_1_q), .clk(clk), .clr(reset));
  Multiplexer #(.select(3), .disabled(0), .enable("false")) multiplexer_1 (
    .in0(way), .in1(nia[0]), .in2(nia[1]), .in3(nia[2]), .in4(1'b0), .in5(1'b1), .out(multiplexer_1_out),
    .sel(rom_2_data));  // open: in6, in7
  Multiplexer #(.select(2), .width(5), .disabled(0), .enable("false")) multiplexer_2 (
    .in0(set), .in1(cto), .in2({5{1'b0}}), .out(multiplexer_2_out), .sel(rom_3_data));  // open: in3
  Register #(.width(16)) register_2 (.D(register_1_q), .en(hit), .Q(register_2_q), .clk(clk), .clr(reset));
  Comparator #(.width(16), .mode("unsigned")) comparator_1 (
    .a(in_3), .b(inst[15:0]), .eq(comparator_1_eq));  // open: gt, lt
  Comparator #(.width(7), .mode("unsigned")) comparator_2 (
    .a(ciclo), .b(7'b0011001), .gt(comparator_2_gt));  // open: eq, lt
  Comparator #(.width(16), .mode("unsigned")) comparator_3 (
    .a(in_3), .b(register_1_q), .eq(comparator_3_eq));  // open: gt, lt
  Comparator #(.width(16), .mode("unsigned")) comparator_4 (
    .a(in_3), .b(register_2_q), .eq(comparator_4_eq));  // open: gt, lt
  not not_1 (err1, comparator_1_eq);
  Comparator #(.width(5), .mode("unsigned")) comparator_5 (
    .a(set), .b(multiplexer_2_out), .eq(comparator_5_eq));  // open: gt, lt
  or or_1 (or_1_out, comparator_3_eq, comparator_4_eq);
  xnor xnor_1 (xnor_1_out, way, multiplexer_1_out);
  and and_1 (err5, comparator_2_gt, or_1_out, hit);
  not not_2 (not_2_out, err5);
  not not_3 (err2, xnor_1_out);
  not not_4 (err3, comparator_5_eq);
  Comparator #(.width(7), .mode("unsigned")) comparator_6 (
    .a(ciclo), .b(7'b1110111), .eq(comparator_6_eq));  // open: gt, lt
  and and_2 (and_2_out, ~rom_1_data, ~hit);  // AND_Gate
  and and_3 (fin, comparator_6_eq, check);
  and and_4 (and_4_out, not_2_out, comparator_1_eq, xnor_1_out, comparator_5_eq, hit, rom_1_data);
  or or_2 (check, and_4_out, and_2_out);
  xor xor_1 (err4, rom_1_data, hit);
  and and_5 (and_5_out, Q0, Q1_plus);
  // Probe on priority_encoder_1_out
  Priority_Encoder #(.disabled(0)) priority_encoder_1 (
    .in1(err1), .in2(err2), .in3(err3), .in4(err4), .in5(err5), .out(priority_encoder_1_out),
    .en_in(and_5_out));  // open: in0, in6, in7, gs, en_out
  Comparator #(.width(5)) comparator_7 (.a(nia[7:3]), .b({5{1'b0}}), .eq(comparator_7_eq));  // open: gt, lt
  Register #(.width(3)) register_3 (
    .D(priority_encoder_1_out), .en(and_5_out), .Q(register_3_q), .clk(clk), .clr(reset));
  Multiplexer #(.width(5), .disabled(0), .enable("false")) multiplexer_3 (
    .in0(nia[7:3]), .in1(5'b00001), .out(cto), .sel(comparator_7_eq));
  and and_6 (count, Q0, ~fin, check);  // AND_Gate
  and and_7 (and_7_out, Q0, ~check);  // AND_Gate
  and and_8 (and_8_out, Q0, check, fin);
  and and_9 (and_9_out, ~Q0r, ~Q1, ~Q2);  // AND_Gate
  Multiplexer #(.width(3), .disabled(0), .enable("false")) multiplexer_4 (
    .in0(priority_encoder_1_out), .in1(register_3_q), .out(ERR), .sel(Q1));
  D_Flip_Flop u_Q0 (.clk(clk), .D(count), .Q(Q0r), .preset(reset));  // open: Qn, en, reset
  D_Flip_Flop u_Q1 (.clk(clk), .D(Q1_plus), .Q(Q1), .reset(reset));  // open: Qn, preset, en
  or or_3 (Q1_plus, and_7_out, Q1);
  D_Flip_Flop u_Q2 (.clk(clk), .D(OK), .Q(Q2), .reset(reset));  // open: Qn, preset, en
  or or_4 (OK, and_8_out, Q2);
  or or_5 (Q0, and_9_out, Q0r);

  // Other names for the same wires on the sheet: COD_ERR[2:0] = ERR; Q0_plus = count; via = nia[0]; via2 = nia[1];
  //   via3 = nia[2]; Q2_plus = OK

  // Notes on the sheet:
  //   contents of rom_1 (hex, n*v repeats v):
  //   12*0 1 12*0 1 12*0 1 1 12*0 1 12*0 1 12*0 1 1 12*0 1 12*0 1 12*0 1 1
  //   contents of rom_2 (hex, n*v repeats v):
  //   12*0 4 12*0 5 12*0 4 1 12*0 4 12*0 5 12*0 4 2 12*0 5 12*0 4 12*0 5 3
  //   contents of rom_3 (hex, n*v repeats v):
  //   12*0 2 12*0 2 12*0 2 2 12*0 1 12*0 1 12*0 1 1 12*0 2 12*0 2 12*0 2 2
  //   parche para evitar cto 0 (se pasa al 1)
  //   Apaño para que funcione sin pulsar reset
  //   Unidad de Control - Estados codificados en unario
  //   1 inst erronea o dir. no alineada
  //   2 vía erronea
  //   3 cto. erroneo
  //   4 hit/miss erroneo
  //   5 dir. repetida
endmodule
